# Fritzing sketch Antifurto (saved by Fritzing 0.7.4b)
breadboards: 1

parts:
  Arduino1 = Arduino
  Componente1 = Arduino Cellular Shield
  Power_plug1 = Power plug
  K_GSM = Relay [part_number=FRS1B-S package=THT]
  K1 = Relay [part_number=FRS1B-S package=THT]
  S1 = Pushbutton [package=THT]
  IR2 = Infrared Proximity Sensor
  IR1 = Infrared Proximity Sensor
  J1 = Piezo Speaker

nets:
  GND: Arduino1.GND, Componente1.GND, Power_plug1.GND, K_GSM.COIL1, S1.leg0, IR2.GND, IR1.GND, J1.pin1
  N1: Arduino1.D12, S1.leg1
  N2: Arduino1.D11, J1.pin2
  N3: Arduino1.D9, IR2.Vout
  N4: Arduino1.D8, IR1.Vout
  N5: Arduino1.D5, K1.B
  N6: Arduino1.D4, K_GSM.COIL2
  N7: Arduino1.D3, Componente1.TX-O
  N8: Arduino1.D2, Componente1.RX-I
  VCC: Arduino1.+5V, Power_plug1.VCC, K_GSM.C1, K_GSM.C2, IR2.Vcc, IR1.Vcc
  N9: Componente1.5V, K_GSM.B
  N10: K1.C1, K1.C2
